# Fritzing sketch water-temperature-sensor (saved by Fritzing 0.9.3b)
breadboards: 1

parts:
  Part1 = Adafruit Thermocouple Amplifier MAX31855 [part_number="Adafruit #269"]
  WeMos_D1_Mini1 = WeMos D1 Mini  # not connected
  J1 = male pin header, 8 pins [form="♂ (male)"]
  J2 = male pin header, 8 pins [form="♂ (male)"]
  R1 = Resistor [tolerance=±1% resistance=10k package=THT]

nets:
  N1: Part1.+3V3, J2.pin8
  N2: Part1.GND, Part1.CS, J2.pin7, R1.Pin_0
  N3: Part1.DO, J2.pin5
  N4: Part1.CLK, J2.pin4
  N5: J1.pin7, R1.Pin_1

custom parts:
  Adafruit Thermocouple Amplifier MAX31855: Thermocouples are very sensitive, requiring a good amplifier with a cold-compensation reference. The MAX31855K does everything for you, and can be easily interfaced with any microcontroller, even one without an analog input. This breakout board has the chip itself, a 3.3V regulator with 10uF bypass capacitors and level shifting circuitry, all assembled and tested. Comes with a 2 pin terminal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
  WeMos D1 Mini: The D1 mini is a mini wifi board based on ESP-8266EX.
